// Logisim project combinational-logic.circ as structural Verilog: 2 circuits, main circuit cache-entry
module main (
  input  [7:0] address,
  input  read_enable,
  input  [31:0] ROM_data_in,
  output [7:0] data_out,
  output [5:0] ROM_read_address,
  output ROM_read_enable
);

  Multiplexer #(.select(2), .width(8), .enable("false")) multiplexer_1 (
    .in0(ROM_data_in[7:0]), .in1(ROM_data_in[15:8]), .in2(ROM_data_in[23:16]), .in3(ROM_data_in[31:24]),
    .out(data_out), .sel(address[1:0]));

  assign ROM_read_address = address[7:2];
  assign ROM_read_enable = read_enable;

  // Notes on the sheet:
  //   ROM_read_address: pull=down
  //   ROM_read_enable: pull=down
  //   data_out: pull=down
endmodule

module cache_entry (
  input  [31:0] data_in,
  input  [3:0] tag,
  input  clock,
  output [31:0] data_out,
  output miss
);
endmodule
